// Digital circuit Demux_1Entrada.dig as structural Verilog
module Demux_1Entrada (
  input  D0,
  input  Sel1,
  input  Sel2,
  output out_1,
  output out_2,
  output out_3,
  output out_4
);

  wire not_1_out, not_2_out;

  not not_1 (not_1_out, Sel1);
  not not_2 (not_2_out, Sel2);
  and and_1 (out_1, D0, Sel1, Sel2);
  and and_2 (out_2, D0, Sel1, not_2_out);
  and and_3 (out_3, D0, not_1_out, Sel2);
  and and_4 (out_4, D0, not_1_out, not_2_out);
endmodule
