// Digital circuit Registro_PinIO.dig as structural Verilog
module Registro_PinIO (
  input  D3,
  input  En,
  input  C,
  input  Set,
  input  D2,
  input  D1,
  input  D0,
  input  Ent3,
  input  En_2,
  input  C_2,
  input  Set_2,
  input  Ent2,
  input  Ent1,
  input  Ent0,
  input  En_3,
  input  C_3,
  input  Set_3,
  input  Clock,
  input  Clock_2,
  input  Clock_3,
  input  in_29,
  input  in_30,
  input  in_31,
  input  in_32,
  output out_18,
  output out_19,
  output out_20,
  output out_21,
  output out_25,
  output out_26,
  output out_27,
  output out_28
);

  wire D0_t, D0E, D0S, D1_t, D1E, D1S, D2_t, D2E, D2S, D3_t, D3E, D3S, multiplexer_1_out, multiplexer_2_out,
       multiplexer_3_out, multiplexer_4_out, multiplexer_5_out, multiplexer_6_out, multiplexer_7_out,
       multiplexer_8_out, multiplexer_9_out, multiplexer_10_out, multiplexer_11_out, multiplexer_12_out;

  Multiplexer multiplexer_1 (.sel(En_2), .in_0(D3E), .in_1(Ent3), .out(multiplexer_1_out));
  D_FF_AS d_ff_as_1 (.Set(Set_2), .D(multiplexer_1_out), .C(Clock_2), .Clr(C_2), .Q(D3E));  // open: nQ
  assign out_28 = D0_t ? D0E : 1'bz;  // Driver driver_1
  assign out_25 = D1_t ? D1E : 1'bz;  // Driver driver_2
  assign out_26 = D2_t ? D2E : 1'bz;  // Driver driver_3
  assign out_27 = D3_t ? D3E : 1'bz;  // Driver driver_4
  Multiplexer multiplexer_2 (.sel(En_2), .in_0(D2E), .in_1(Ent2), .out(multiplexer_2_out));
  D_FF_AS d_ff_as_2 (.Set(Set_2), .D(multiplexer_2_out), .C(Clock_2), .Clr(C_2), .Q(D2E));  // open: nQ
  Multiplexer multiplexer_3 (.sel(En_2), .in_0(D1E), .in_1(Ent1), .out(multiplexer_3_out));
  assign D0S = ~D0_t ? in_29 : 1'bz;  // DriverInvSel driverinvsel_1
  assign D1S = ~D1_t ? in_30 : 1'bz;  // DriverInvSel driverinvsel_2
  assign D2S = ~D2_t ? in_31 : 1'bz;  // DriverInvSel driverinvsel_3
  assign D3S = ~D3_t ? in_32 : 1'bz;  // DriverInvSel driverinvsel_4
  D_FF_AS d_ff_as_3 (.Set(Set_2), .D(multiplexer_3_out), .C(Clock_2), .Clr(C_2), .Q(D1E));  // open: nQ
  Multiplexer multiplexer_4 (.sel(En_2), .in_0(D0E), .in_1(Ent0), .out(multiplexer_4_out));
  D_FF_AS d_ff_as_4 (.Set(Set_2), .D(multiplexer_4_out), .C(Clock_2), .Clr(C_2), .Q(D0E));  // open: nQ
  Multiplexer multiplexer_5 (.sel(En), .in_0(D3_t), .in_1(D3), .out(multiplexer_5_out));
  D_FF_AS d_ff_as_5 (.Set(Set), .D(multiplexer_5_out), .C(Clock), .Clr(C), .Q(D3_t));  // open: nQ
  Multiplexer multiplexer_6 (.sel(En_3), .in_0(out_18), .in_1(D3S), .out(multiplexer_6_out));
  Multiplexer multiplexer_7 (.sel(En), .in_0(D2_t), .in_1(D2), .out(multiplexer_7_out));
  D_FF_AS d_ff_as_6 (.Set(Set), .D(multiplexer_7_out), .C(Clock), .Clr(C), .Q(D2_t));  // open: nQ
  D_FF_AS d_ff_as_7 (.Set(Set_3), .D(multiplexer_6_out), .C(Clock_3), .Clr(C_3), .Q(out_18));  // open: nQ
  Multiplexer multiplexer_8 (.sel(En_3), .in_0(out_19), .in_1(D2S), .out(multiplexer_8_out));
  Multiplexer multiplexer_9 (.sel(En), .in_0(D1_t), .in_1(D1), .out(multiplexer_9_out));
  D_FF_AS d_ff_as_8 (.Set(Set), .D(multiplexer_9_out), .C(Clock), .Clr(C), .Q(D1_t));  // open: nQ
  D_FF_AS d_ff_as_9 (.Set(Set_3), .D(multiplexer_8_out), .C(Clock_3), .Clr(C_3), .Q(out_19));  // open: nQ
  Multiplexer multiplexer_10 (.sel(En), .in_0(D0_t), .in_1(D0), .out(multiplexer_10_out));
  Multiplexer multiplexer_11 (.sel(En_3), .in_0(out_20), .in_1(D1S), .out(multiplexer_11_out));
  D_FF_AS d_ff_as_10 (.Set(Set), .D(multiplexer_10_out), .C(Clock), .Clr(C), .Q(D0_t));  // open: nQ
  D_FF_AS d_ff_as_11 (.Set(Set_3), .D(multiplexer_11_out), .C(Clock_3), .Clr(C_3), .Q(out_20));  // open: nQ
  Multiplexer multiplexer_12 (.sel(En_3), .in_0(out_21), .in_1(D0S), .out(multiplexer_12_out));
  D_FF_AS d_ff_as_12 (.Set(Set_3), .D(multiplexer_12_out), .C(Clock_3), .Clr(C_3), .Q(out_21));  // open: nQ

  // Notes on the sheet:
  //   Clock: Hz: 60
  //   Clock_2: Hz: 60
  //   Clock_3: Hz: 60
  //   Registro de almacenamiento
  //   (Entrada)
  //   Registro de configuracion
  //   (Entrada/salida)
  //   Registro de control
  //   (Salida)
endmodule
